// Digital circuit Template-04.dig as structural Verilog
module Template_04 (
  input  [6:0] In,
  output [6:0] Output
);

  wire not_1_out, not_2_out, not_3_out, xor_2_out, xor_3_out, xor_4_out;
  wire [6:0] ham;

  assign Output = In ^ ham;  // XOr xor_1, 7 bits wide
  xor xor_2 (xor_2_out, In[3], In[4], In[5], In[6]);
  xor xor_3 (xor_3_out, In[1], In[2], In[5], In[6]);
  xor xor_4 (xor_4_out, In[0], In[2], In[4], In[6]);
  not not_1 (not_1_out, xor_4_out);
  not not_2 (not_2_out, xor_3_out);
  not not_3 (not_3_out, xor_2_out);
  and and_1 (ham[6], xor_2_out, xor_3_out, xor_4_out);
  and and_2 (ham[5], xor_2_out, xor_3_out, not_1_out);
  and and_3 (ham[4], xor_2_out, not_2_out, xor_4_out);
  and and_4 (ham[3], xor_2_out, not_2_out, not_1_out);
  and and_5 (ham[2], not_3_out, xor_3_out, xor_4_out);
  and and_6 (ham[1], not_3_out, xor_3_out, not_1_out);
  and and_7 (ham[0], not_3_out, not_2_out, xor_4_out);
endmodule
