// Digital circuit TEMPLATE ver.Multi-Cycle.dig as structural Verilog
module TEMPLATE_ver_Multi_Cycle (
  input  [7:0] M,
  input  [7:0] N,
  input  [12:0] progIN,
  input  reset,
  input  progLoad,
  input  start,
  input  result,
  input  clk,
  output valid,
  output done,
  output [7:0] \output ,
  output [7:0] out_12,
  output [12:0] out_13,
  output [7:0] out_14,
  output [7:0] out_15,
  output [7:0] out_16
);

  wire _00, _0000, _00000, _00001, _0001, _01, _00010, _0010, _10, _00011, _0011, _11, _00100, _0100, _00101,
       _0101, _00110, _0110, _00111, _0111, _01000, _1000, _01001, _1001, _01010, _1010, _01011, _1011,
       _01100, _1100, _01101, _1101, _01110, _1110, _01111, _1111, _10000, _10001, _10010, _10011, _10100,
       _10101, _10110, _10111, _11000, _11001, _11010, _11011, _11100, _11101, _11110, _11111, ALU,
       and_1_out, and_2_out, and_3_out, and_5_out, and_6_out, and_7_out, and_8_out, and_9_out, and_10_out,
       and_11_out, and_12_out, and_13_out, and_14_out, and_15_out, and_18_out, and_19_out, and_20_out,
       and_21_out, and_23_out, d_ff_3_nq, d_ff_4_q, d_ff_5_q, en_rRAM, enA, enB, enC, eq, eq_t, gr, gt,
       isPrime_d, jump, jumpOp, le, lt, move, multiplexer_1_out, multiplexer_2_out, multiplexer_3_out,
       multiplexer_4_out, multiplexer_8_out, multiplexer_13_out, multiplexer_14_out, multiplexer_15_out,
       multiplexer_16_out, not_1_out, not_3_out, not_4_out, or_1_out, or_2_out, or_3_out, or_4_out, or_5_out,
       or_6_out, or_7_out, or_8_out, or_9_out, or_10_out, or_11_out, or_12_out, or_13_out, or_14_out,
       or_15_out, or_16_out, or_17_out, or_19_out, or_20_out, or_21_out, or_22_out, or_24_out, or_27_out,
       or_28_out, or_29_out, P_a, P_b, Q_a, Q_b, Q_c, Q_d, r_cnt_eq_16, r_cnt_gt_16, r_cnt_lt_16,
       result_cnt_eq_16, result_cnt_gt_16, result_cnt_lt_16, start_t;
  wire [2:1] bitcount_4_out;
  wire [3:1] bitcount_2_out, bitcount_3_out;
  wire [4:0] bitcount_1_out;
  wire [7:0] A, A_B, A_lt__lt_B, AND, cnt, DIFF, DIV, MOD, MUL, multiplexer_5_out, multiplexer_6_out,
       multiplexer_7_out, multiplexer_9_out, multiplexer_10_out, multiplexer_11_out, OR, pRAM_operand, r_cnt,
       result_cnt, rRAM_operand, SUM, val, XOR;
  wire [12:8] pRAM_d1;

  or or_1 (or_1_out, reset, _11111);
  or or_2 (or_2_out, _00, result);
  or or_3 (or_3_out, start, progLoad, reset);
  and and_1 (and_1_out, ~reset, ~result);  // And
  or or_4 (or_4_out, start, progLoad, reset);
  or or_5 (or_5_out, _0101, _0111, _1000, _0110);
  CounterPreset #(.maxValue(256), .Bits(8)) pc (
    .en(or_5_out), .C(clk), .dir(1'b0), .in(out_13[7:0]), .ld(jump), .clr(or_1_out), .out(out_12));  // open: ovf
  Counter #(.Bits(8)) u_result_cnt (.en(_01), .C(clk), .clr(or_2_out), .out(result_cnt));  // open: ovf
  Comparator #(.Bits(8)) comparator_1 (
    .a(result_cnt), .b(8'h10), .gt(result_cnt_gt_16), .eq(result_cnt_eq_16), .lt(result_cnt_lt_16));
  not not_1 (not_1_out, result_cnt_eq_16);
  Multiplexer #(.Selector_Bits(2)) multiplexer_1 (
    .sel({P_a, P_b}), .in_0(1'b0), .in_1(result_cnt_eq_16), .in_2(and_1_out), .in_3(1'b0),
    .out(multiplexer_1_out));
  Multiplexer #(.Selector_Bits(2)) multiplexer_2 (
    .sel({P_a, P_b}), .in_0(result), .in_1(not_1_out), .in_2(result), .in_3(1'b0), .out(multiplexer_2_out));
  and and_2 (and_2_out, ~or_3_out, multiplexer_1_out);  // And
  and and_3 (and_3_out, ~or_4_out, multiplexer_2_out);  // And
  or or_6 (or_6_out, reset, ~progLoad);  // Or
  D_FF d_ff_1 (.D(and_2_out), .C(clk), .Q(P_a));  // open: nQ
  D_FF d_ff_2 (.D(and_3_out), .C(clk), .Q(P_b));  // open: nQ
  CounterPreset #(.maxValue(256), .Bits(8)) u_cnt (
    .en(progLoad), .C(clk), .dir(1'b0), .in({8{1'b0}}), .ld(1'b0), .clr(or_6_out), .out(cnt));  // open: ovf
  Decoder #(.Selector_Bits(2)) decoder_1 (.sel({P_a, P_b}), .out_0(_00), .out_1(_01), .out_2(_10), .out_3(_11));
  CounterPreset #(.maxValue(256), .Bits(8)) u_r_cnt (
    .en(_0011), .C(clk), .dir(1'b0), .in({8{1'b0}}), .ld(1'b0), .clr(r_cnt_eq_16), .out(r_cnt));  // open: ovf
  D_FF d_ff_3 (.D(start), .C(clk), .nQ(d_ff_3_nq));  // open: Q
  D_FF d_ff_4 (.D(start), .C(clk), .Q(d_ff_4_q));  // open: nQ
  D_FF d_ff_5 (.D(d_ff_3_nq), .C(clk), .Q(d_ff_5_q));  // open: nQ
  Comparator #(.Bits(8)) u_r_cnt_eq_16 (.a(r_cnt), .b(8'h10), .gt(r_cnt_gt_16), .eq(r_cnt_eq_16), .lt(r_cnt_lt_16));
  and and_4 (start_t, d_ff_4_q, d_ff_5_q);
  and and_5 (and_5_out, lt, _10111);
  or or_7 (or_7_out, reset, start, progLoad);
  Multiplexer multiplexer_3 (.sel(_0111), .in_0(1'b0), .in_1(and_5_out), .out(multiplexer_3_out));
  or or_8 (or_8_out, start, and_6_out);
  RS_FF_AS rs_ff_as_1 (.S(_11111), .R(or_7_out), .Q(valid));  // open: nQ
  Register register_1 (.D(multiplexer_3_out), .C(clk), .en(or_8_out), .Q(le));
  Multiplexer multiplexer_4 (.sel(_0111), .in_0(1'b0), .in_1(or_10_out), .out(multiplexer_4_out));
  Register register_2 (.D(multiplexer_4_out), .C(clk), .en(or_9_out), .Q(eq_t));
  or or_9 (or_9_out, start, and_7_out);
  and and_6 (and_6_out, _0111, _10111);
  and and_7 (and_7_out, _0111, or_11_out);
  or or_10 (or_10_out, and_10_out, and_9_out);
  Multiplexer #(.Selector_Bits(2), .Bits(8)) multiplexer_5 (
    .sel({en_rRAM, _01010}), .in_0(r_cnt), .in_1(out_13[7:0]), .in_2(out_13[7:0]), .in_3({8{1'b0}}),
    .out(multiplexer_5_out));
  and and_8 (and_8_out, gt, _10111);
  and and_9 (and_9_out, _11101, isPrime_d);
  and and_10 (and_10_out, eq, _10111);
  or or_11 (or_11_out, _11101, _10111);
  or or_12 (or_12_out, _10, result_cnt_eq_16);
  Multiplexer #(.Bits(8)) multiplexer_6 (.sel(_01001), .in_0(cnt), .in_1(out_13[7:0]), .out(multiplexer_6_out));
  or or_13 (or_13_out, en_rRAM, _0011);
  Multiplexer #(.Bits(8)) multiplexer_7 (.sel(en_rRAM), .in_0({8{1'b0}}), .in_1(val), .out(multiplexer_7_out));
  or or_14 (or_14_out, reset, start, progLoad, result);
  Multiplexer multiplexer_8 (.sel(_0111), .in_0(1'b0), .in_1(and_8_out), .out(multiplexer_8_out));
  or or_15 (or_15_out, start, and_11_out);
  ROM #(.AddrBits(8)) isPrime (.A(out_14), .sel(1'b1), .D(isPrime_d));
  Seven_Seg_Hex seven_seg_hex_1 (.d(\output [7:4]), .dp(1'b0));
  RS_FF_AS rs_ff_as_2 (.S(or_12_out), .R(or_14_out), .Q(done));  // open: nQ
  RAMDualAccess #(.AddrBits(8), .Bits(13)) pRAM (
    .str(progLoad), .C(clk), .ld(_01001), .A1(multiplexer_6_out), .Din1(progIN), .A2(out_12),
    .D1({pRAM_d1, pRAM_operand}), .D2(out_13));
  RAMDualAccess #(.AddrBits(8), .Bits(8)) rRAM (
    .str(or_13_out), .C(clk), .ld(_01010), .A1(multiplexer_5_out), .Din1(multiplexer_7_out), .A2(result_cnt),
    .D1(rRAM_operand), .D2(\output ));
  Register register_3 (.D(multiplexer_8_out), .C(clk), .en(or_15_out), .Q(gr));
  Seven_Seg_Hex seven_seg_hex_2 (.d(\output [3:0]), .dp(1'b0));
  and and_11 (and_11_out, _0111, _10111);
  or or_16 (or_16_out, eq_t, gr);
  and and_12 (and_12_out, _01101, eq_t);
  and and_13 (and_13_out, _01110, gr);
  and and_14 (and_14_out, _01111, le);
  and and_15 (and_15_out, _10000, or_16_out);
  Comparator #(.Signed("true"), .Bits(8)) comparator_2 (.a(out_14), .b(out_15), .gt(gt), .eq(eq), .lt(lt));
  or or_17 (or_17_out, _01100, and_12_out, and_13_out, and_14_out, and_15_out);
  and and_16 (jump, or_17_out, _0110);
  Multiplexer #(.Bits(8)) multiplexer_9 (.sel(reset), .in_0(val), .in_1({8{1'b0}}), .out(multiplexer_9_out));
  Multiplexer #(.Bits(8)) multiplexer_10 (.sel(reset), .in_0(val), .in_1({8{1'b0}}), .out(multiplexer_10_out));
  Multiplexer #(.Bits(8)) multiplexer_11 (.sel(reset), .in_0(val), .in_1({8{1'b0}}), .out(multiplexer_11_out));
  Register #(.Bits(8)) accA (.D(multiplexer_9_out), .C(clk), .en(enA), .Q(out_14));
  Register #(.Bits(8)) accB (.D(multiplexer_10_out), .C(clk), .en(enB), .Q(out_15));
  Register #(.Bits(8)) regC (.D(multiplexer_11_out), .C(clk), .en(enC), .Q(out_16));
  assign AND = out_14 & out_15;  // And and_17, 8 bits wide
  assign OR = out_14 | out_15;  // Or or_18, 8 bits wide
  assign XOR = out_14 ^ out_15;  // XOr xor_1, 8 bits wide
  Add #(.Bits(8)) add_1 (.a(out_14), .b(out_15), .c_i(1'b0), .s(SUM));  // open: c_o
  Sub #(.Bits(8)) sub_1 (.a(out_14), .b(out_15), .c_i(1'b0), .s(DIFF));  // open: c_o
  Mul #(.Bits(4)) mul_1 (.a(out_14[3:0]), .b(out_15[3:0]), .mul(MUL));
  Div #(.Bits(8)) divide (.a(out_14), .b(out_15), .q(DIV));  // open: r
  Div #(.Bits(8)) u_mod (.a(out_14), .b(out_15), .r(MOD));  // open: q
  assign A = ~out_14;  // Not not_2, 8 bits wide
  BarrelShifter #(.Bits(8), .barrelShifterMode("arithmetic")) barrelshifter_1 (
    .in(out_14), .shift({1'b0, out_15[2:0]}), .out(A_lt__lt_B));
  LookUpTable #(.Bits(8)) exponent (
    .in0(out_15[0]), .in1(out_15[1]), .in2(out_15[2]), .in3(out_14[0]), .in4(out_14[1]), .in5(out_14[2]),
    .out(A_B));
  Multiplexer #(.Selector_Bits(5), .Bits(8)) multiplexer_12 (
    .sel(out_13[12:8]), .in_0({8{1'b0}}), .in_1(out_13[7:0]), .in_2(out_13[7:0]), .in_3(out_15),
    .in_4(out_14), .in_5(out_14), .in_6(out_16), .in_7(M), .in_8(N), .in_9(pRAM_operand),
    .in_10(rRAM_operand), .in_11(out_14), .in_12({8{1'b0}}), .in_13({8{1'b0}}), .in_14({8{1'b0}}),
    .in_15({8{1'b0}}), .in_16({8{1'b0}}), .in_17(SUM), .in_18(DIFF), .in_19(MUL), .in_20(DIV), .in_21(MOD),
    .in_22(A_B), .in_23({8{1'b0}}), .in_24(A), .in_25(AND), .in_26(OR), .in_27(XOR), .in_28(A_lt__lt_B),
    .in_29({8{1'b0}}), .in_30({8{1'b0}}), .in_31({8{1'b0}}), .out(val));
  or or_19 (or_19_out, _11110, _11111);
  and and_18 (and_18_out, ~start, ~reset);  // And
  Multiplexer #(.Selector_Bits(4)) multiplexer_13 (
    .sel({Q_a, Q_b, Q_c, Q_d}), .in_0(1'b0), .in_1(1'b0), .in_2(1'b0), .in_3(1'b0), .in_4(or_19_out),
    .in_5(1'b0), .in_6(1'b0), .in_7(1'b0), .in_8(1'b0), .in_9(and_18_out), .in_10(1'b0), .in_11(1'b0),
    .in_12(1'b0), .in_13(1'b0), .in_14(1'b0), .in_15(1'b0), .out(multiplexer_13_out));
  BitCount #(.Bits(16)) bitcount_1 (
    .in({_11100, _11011, _11010, _11001, _11000, _10110, _10101, _10100, _10011, _10010, _10001, _01010, _01001, _00110, _00011, _00001}),
    .out(bitcount_1_out));
  D_FF d_ff_6 (.D(multiplexer_13_out), .C(clk), .Q(Q_a));  // open: nQ
  and and_19 (and_19_out, bitcount_1_out[0], or_20_out);
  or or_20 (or_20_out, _0101, _0111);
  or or_21 (or_21_out, _00010, _00100);
  or or_22 (or_22_out, _00101, _00111, _01000);
  and and_20 (and_20_out, or_21_out, _0101);
  and and_21 (and_21_out, or_22_out, _0101);
  or or_23 (enA, and_19_out, reset);
  or or_24 (or_24_out, ALU, jumpOp, move);
  or or_25 (enB, reset, and_20_out);
  or or_26 (enC, reset, and_21_out);
  and and_22 (en_rRAM, _01011, _0101);
  Multiplexer #(.Selector_Bits(4)) multiplexer_14 (
    .sel({Q_a, Q_b, Q_c, Q_d}), .in_0(start), .in_1(start), .in_2(1'b0), .in_3(1'b0), .in_4(or_24_out),
    .in_5(1'b1), .in_6(1'b1), .in_7(1'b1), .in_8(1'b1), .in_9(start), .in_10(1'b0), .in_11(1'b0),
    .in_12(1'b0), .in_13(1'b0), .in_14(1'b0), .in_15(1'b0), .out(multiplexer_14_out));
  D_FF d_ff_7 (.D(multiplexer_14_out), .C(clk), .Q(Q_b));  // open: nQ
  or or_27 (or_27_out, ALU, jumpOp);
  not not_3 (not_3_out, r_cnt_eq_16);
  Multiplexer #(.Selector_Bits(4)) multiplexer_15 (
    .sel({Q_a, Q_b, Q_c, Q_d}), .in_0(reset), .in_1(reset), .in_2(1'b1), .in_3(not_3_out), .in_4(or_27_out),
    .in_5(1'b0), .in_6(1'b0), .in_7(1'b0), .in_8(1'b0), .in_9(reset), .in_10(1'b0), .in_11(1'b0),
    .in_12(1'b0), .in_13(1'b0), .in_14(1'b0), .in_15(1'b0), .out(multiplexer_15_out));
  D_FF d_ff_8 (.D(multiplexer_15_out), .C(clk), .Q(Q_c));  // open: nQ
  or or_28 (or_28_out, ALU, _11111, move);
  and and_23 (and_23_out, ~start, ~reset);  // And
  Multiplexer #(.Selector_Bits(4)) multiplexer_16 (
    .sel({Q_a, Q_b, Q_c, Q_d}), .in_0(progLoad), .in_1(progLoad), .in_2(1'b1), .in_3(not_4_out),
    .in_4(or_28_out), .in_5(1'b0), .in_6(1'b0), .in_7(1'b0), .in_8(1'b0), .in_9(and_23_out), .in_10(1'b0),
    .in_11(1'b0), .in_12(1'b0), .in_13(1'b0), .in_14(1'b0), .in_15(1'b0), .out(multiplexer_16_out));
  not not_4 (not_4_out, r_cnt_eq_16);
  D_FF d_ff_9 (.D(multiplexer_16_out), .C(clk), .Q(Q_d));  // open: nQ
  Decoder #(.Selector_Bits(4)) decoder_2 (
    .sel({Q_a, Q_b, Q_c, Q_d}), .out_0(_0000), .out_1(_0001), .out_2(_0010), .out_3(_0011), .out_4(_0100),
    .out_5(_0101), .out_6(_0110), .out_7(_0111), .out_8(_1000), .out_9(_1001), .out_10(_1010),
    .out_11(_1011), .out_12(_1100), .out_13(_1101), .out_14(_1110), .out_15(_1111));
  or or_29 (or_29_out, _1000, _0111, _0110, _0101, _0100);
  BitCount #(.Bits(13)) bitcount_2 (
    .in({_10001, _10010, _10011, _10100, _10101, _10110, _10111, _11000, _11001, _11010, _11011, _11100, _11101}),
    .out({bitcount_2_out, ALU}));
  Demultiplexer #(.Selector_Bits(5)) demultiplexer_1 (
    .sel(out_13[12:8]), .in(or_29_out), .out_0(_00000), .out_1(_00001), .out_2(_00010), .out_3(_00011),
    .out_4(_00100), .out_5(_00101), .out_6(_00110), .out_7(_00111), .out_8(_01000), .out_9(_01001),
    .out_10(_01010), .out_11(_01011), .out_12(_01100), .out_13(_01101), .out_14(_01110), .out_15(_01111),
    .out_16(_10000), .out_17(_10001), .out_18(_10010), .out_19(_10011), .out_20(_10100), .out_21(_10101),
    .out_22(_10110), .out_23(_10111), .out_24(_11000), .out_25(_11001), .out_26(_11010), .out_27(_11011),
    .out_28(_11100), .out_29(_11101), .out_30(_11110), .out_31(_11111));
  BitCount #(.Bits(12)) bitcount_3 (
    .in({_00000, _00001, _00010, _00011, _00100, _00101, _00110, _00111, _01000, _01001, _01010, _01011}),
    .out({bitcount_3_out, move}));
  BitCount #(.Bits(5)) bitcount_4 (.in({_01100, _01101, _01110, _01111, _10000}), .out({bitcount_4_out, jumpOp}));

  // Other names for the same wires on the sheet: accA[7:0] = out_14; accB[7:0] = out_15; future = _11110;
  //   operand[7:0] = out_13[7:0]; opcode[4:0] = out_13[12:8]; pc[7:0] = out_12; regC[7:0] = out_16; stop = _11111

  // Notes on the sheet:
  //   Program load & reset
  //   Jump control unit
  //   Ram Unit
  //   contents of isPrime (hex, n*v repeats v):
  //   0,0,1,1,0,1,0,1,0,0,0,1,0,1,0,0,0,1,0,1,0,0,0,1,5*0,1,0,1,5*0
  //   ,1,0,0,0,1,0,1,0,0,0,1,5*0,1,5*0,1,0,1,5*0,1,0,0,0,1,0,1,5*0,1
  //   ,0,0,0,1,5*0,1,7*0,1,0,0,0,1,0,1,0,0,0,1,0,1,0,0,0,1,13*0,1,0,0,0
  //   ,1,5*0,1,0,1,9*0,1,0,1,5*0,1,5*0,1,0,0,0,1,5*0,1,5*0,1,0,1,9*0
  //   ,1,0,1,0,0,0,1,0,1,11*0,1,11*0,1,0,0,0,1,0,1,0,0,0,1,5*0,1,0,1
  //   ,9*0,1
  //   Register unit
  //   ALU unit
  //   contents of exponent (hex, n*v repeats v):
  //   1,0,a0000,a00000,0,40000,0,0,9*1,2,4,8,10,20,40,80,1,3,9,1b,51
  //   ,f3,d9,8b,1,4,10,40,4*0,1,5,19,7d,71,35,9,2d,1,6,24,d8,10,60,40
  //   ,80,1,7,31,57,61,a7,91,f7,0,0,0,1,0,0,0,1,0,1,5*0,1,0,0,0,1,5*0
  //   ,1,7*0,1,0,0,0,1,0,1,0,0,0,1,0,1,0,0,0,1,13*0,1,0,0,0,1,5*0,1
  //   ,0,1,9*0,1,0,1,5*0,1,5*0,1,0,0,0,1,5*0,1,5*0,1,0,1,9*0,1,0,1,0,0,0
  //   ,1,0,1,11*0,1,11*0,1,0,0,0,1,0,1,0,0,0,1,5*0,1,0,1,9*0,1
  //   State processing unit
endmodule

/* Test case 01_P01T01:
M N progIN reset progLoad start result clk valid done output
0 0 0 0 0 0 0 0 x x x
0 0 0 0 0 0 0 1 x x x
0 0 0 1 0 0 0 0 x x x
0 0 0 1 0 0 0 1 0 0 x
0 0 0 0 0 0 0 0 0 0 x
0 0 0 0 0 0 0 1 0 0 x
0 0 0 0 0 0 0 0 0 0 x
0 0 0 0 0 0 0 1 0 0 x
0 0 0 0 0 0 0 0 0 0 x
0 0 0 0 0 0 0 1 0 0 x
0 0 0 0 0 0 0 0 0 0 x
0 0 0 0 0 0 0 1 0 0 x
0 0 0 0 0 0 0 0 0 0 x
0 0 0 0 0 0 0 1 0 0 x
0 0 0 0 0 0 0 0 0 0 x
0 0 0 0 0 0 0 1 0 0 x
0 0 0 0 0 0 0 0 0 0 x
0 0 0 0 0 0 0 1 0 0 x
0 0 0 0 0 0 0 0 0 0 x
0 0 0 0 0 0 0 1 0 0 x
0 0 0 0 0 0 0 0 0 0 x
0 0 0 0 0 0 0 1 0 0 x
0 0 0 0 0 0 0 0 0 0 x
0 0 0 0 0 0 0 1 0 0 x
0 0 0 0 0 0 0 0 0 0 x
0 0 0 0 0 0 0 1 0 0 x
0 0 0 0 0 0 0 0 0 0 x
0 0 0 0 0 0 0 1 0 0 x
0 0 0 0 0 0 0 0 0 0 x
0 0 0 0 0 0 0 1 0 0 x
0 0 0 0 0 0 0 0 0 0 x
0 0 0 0 0 0 0 1 0 0 x
0 0 0 0 0 0 0 0 0 0 x
0 0 0 0 0 0 0 1 0 0 x
0 0 0 0 0 0 0 0 0 0 x
0 0 0 0 0 0 0 1 0 0 x
0 0 0 0 0 0 0 0 0 0 x
0 0 0 0 0 0 0 1 0 0 x
0 0 0 0 0 0 0 0 0 0 x
0 0 0 0 0 0 0 1 0 0 x
0 0 0 0 0 0 0 0 0 0 x
0 0 0 0 0 0 0 1 0 0 x
0 0 271 0 1 0 0 0 0 0 x
0 0 271 0 1 0 0 1 0 0 x
0 0 565 0 1 0 0 0 0 0 x
0 0 565 0 1 0 0 1 0 0 x
0 0 4352 0 1 0 0 0 0 0 x
0 0 4352 0 1 0 0 1 0 0 x
0 0 2819 0 1 0 0 0 0 0 x
0 0 2819 0 1 0 0 1 0 0 x
0 0 7936 0 1 0 0 0 0 0 x
0 0 7936 0 1 0 0 1 0 0 x
0 0 0 0 0 1 0 0 0 0 x
0 0 0 0 0 1 0 1 0 0 x
0 0 0 0 0 0 0 0 x 0 x
0 0 0 0 0 0 0 1 x 0 x
0 0 0 0 0 0 0 0 x 0 x
0 0 0 0 0 0 0 1 x 0 x
0 0 0 0 0 0 0 0 x 0 x
0 0 0 0 0 0 0 1 x 0 x
0 0 0 0 0 0 0 0 x 0 x
0 0 0 0 0 0 0 1 x 0 x
0 0 0 0 0 0 0 0 x 0 x
0 0 0 0 0 0 0 1 x 0 x
0 0 0 0 0 0 0 0 x 0 x
0 0 0 0 0 0 0 1 x 0 x
0 0 0 0 0 0 0 0 x 0 x
0 0 0 0 0 0 0 1 x 0 x
0 0 0 0 0 0 0 0 x 0 x
0 0 0 0 0 0 0 1 x 0 x
0 0 0 0 0 0 0 0 x 0 x
0 0 0 0 0 0 0 1 x 0 x
0 0 0 0 0 0 0 0 x 0 x
0 0 0 0 0 0 0 1 x 0 x
0 0 0 0 0 0 0 0 x 0 x
0 0 0 0 0 0 0 1 x 0 x
0 0 0 0 0 0 0 0 x 0 x
0 0 0 0 0 0 0 1 x 0 x
0 0 0 0 0 0 0 0 x 0 x
0 0 0 0 0 0 0 1 x 0 x
0 0 0 0 0 0 0 0 x 0 x
0 0 0 0 0 0 0 1 x 0 x
0 0 0 0 0 0 0 0 x 0 x
0 0 0 0 0 0 0 1 x 0 x
0 0 0 0 0 0 0 0 x 0 x
0 0 0 0 0 0 0 1 x 0 x
0 0 0 0 0 0 0 0 x 0 x
0 0 0 0 0 0 0 1 x 0 x
0 0 0 0 0 0 0 0 x 0 x
0 0 0 0 0 0 0 1 x 0 x
0 0 0 0 0 0 0 0 x 0 x
0 0 0 0 0 0 0 1 x 0 x
0 0 0 0 0 0 0 0 x 0 x
0 0 0 0 0 0 0 1 x 0 x
0 0 0 0 0 0 0 0 x 0 x
0 0 0 0 0 0 0 1 x 0 x
0 0 0 0 0 0 0 0 x 0 x
0 0 0 0 0 0 0 1 x 0 x
0 0 0 0 0 0 0 0 x 0 x
0 0 0 0 0 0 0 1 x 0 x
0 0 0 0 0 0 0 0 x 0 x
0 0 0 0 0 0 0 1 x 0 x
0 0 0 0 0 0 0 0 x 0 x
0 0 0 0 0 0 0 1 x 0 x
0 0 0 0 0 0 0 0 x 0 x
0 0 0 0 0 0 0 1 1 0 x
0 0 0 0 0 0 1 0 1 0 x
0 0 0 0 0 0 1 1 1 0 0
0 0 0 0 0 0 0 0 1 0 0
0 0 0 0 0 0 0 1 1 0 0
0 0 0 0 0 0 0 0 1 0 0
0 0 0 0 0 0 0 1 1 0 0
0 0 0 0 0 0 0 0 1 0 0
0 0 0 0 0 0 0 1 1 0 68
0 0 0 0 0 0 0 0 1 0 68
0 0 0 0 0 0 0 1 1 0 0
0 0 0 0 0 0 0 0 1 0 0
0 0 0 0 0 0 0 1 1 0 0
0 0 0 0 0 0 0 0 1 0 0
0 0 0 0 0 0 0 1 1 0 0
0 0 0 0 0 0 0 0 1 0 0
0 0 0 0 0 0 0 1 1 0 0
0 0 0 0 0 0 0 0 1 0 0
0 0 0 0 0 0 0 1 1 0 0
0 0 0 0 0 0 0 0 1 0 0
0 0 0 0 0 0 0 1 1 0 0
0 0 0 0 0 0 0 0 1 0 0
0 0 0 0 0 0 0 1 1 0 0
0 0 0 0 0 0 0 0 1 0 0
0 0 0 0 0 0 0 1 1 0 0
0 0 0 0 0 0 0 0 1 0 0
0 0 0 0 0 0 0 1 1 0 0
0 0 0 0 0 0 0 0 1 0 0
0 0 0 0 0 0 0 1 1 0 0
0 0 0 0 0 0 0 0 1 0 0
0 0 0 0 0 0 0 1 1 0 0
0 0 0 0 0 0 0 0 1 0 0
0 0 0 0 0 0 0 1 1 0 0
0 0 0 0 0 0 0 0 1 0 0
0 0 0 0 0 0 0 1 1 1 x
0 0 0 0 0 0 0 0 1 1 x
0 0 0 0 0 0 0 1 1 1 x
0 0 0 0 0 0 0 0 1 1 x
*/

/* Test case Exponent:
M N progIN reset progLoad start result clk valid done output
0 0 0 0 0 0 0 0 x x x
0 0 0 0 0 0 0 1 x x x
0 0 0b0000100000001 0 1 0 0 0 0 0 x
0 0 0b0000100000001 0 1 0 0 1 0 0 x
0 0 0b0001011111111 0 1 0 0 0 0 0 x
0 0 0b0001011111111 0 1 0 0 1 0 0 x
0 0 0b1011000000000 0 1 0 0 0 0 0 x
0 0 0b1011000000000 0 1 0 0 1 0 0 x
0 0 0b0101100000001 0 1 0 0 0 0 0 x
0 0 0b0101100000001 0 1 0 0 1 0 0 x
0 0 0b0000100000010 0 1 0 0 0 0 0 x
0 0 0b0000100000010 0 1 0 0 1 0 0 x
0 0 0b0001011111111 0 1 0 0 0 0 0 x
0 0 0b0001011111111 0 1 0 0 1 0 0 x
0 0 0b1011000000000 0 1 0 0 0 0 0 x
0 0 0b1011000000000 0 1 0 0 1 0 0 x
0 0 0b0101100000011 0 1 0 0 0 0 0 x
0 0 0b0101100000011 0 1 0 0 1 0 0 x
0 0 0b0000100000011 0 1 0 0 0 0 0 x
0 0 0b0000100000011 0 1 0 0 1 0 0 x
0 0 0b0001011111111 0 1 0 0 0 0 0 x
0 0 0b0001011111111 0 1 0 0 1 0 0 x
0 0 0b1011000000000 0 1 0 0 0 0 0 x
0 0 0b1011000000000 0 1 0 0 1 0 0 x
0 0 0b0101100000111 0 1 0 0 0 0 0 x
0 0 0b0101100000111 0 1 0 0 1 0 0 x
0 0 0b1111111111111 0 1 0 0 0 0 0 x
0 0 0b1111111111111 0 1 0 0 1 0 0 x
0 0 0 0 0 1 0 0 0 0 x
0 0 0 0 0 1 0 1 0 0 x
0 0 0 0 0 0 0 0 x x x
0 0 0 0 0 0 0 1 x x x
0 0 0 0 0 0 0 0 x x x
0 0 0 0 0 0 0 1 x x x
0 0 0 0 0 0 0 0 x x x
0 0 0 0 0 0 0 1 x x x
0 0 0 0 0 0 0 0 x x x
0 0 0 0 0 0 0 1 x x x
0 0 0 0 0 0 0 0 x x x
0 0 0 0 0 0 0 1 x x x
0 0 0 0 0 0 0 0 x x x
0 0 0 0 0 0 0 1 x x x
0 0 0 0 0 0 0 0 x x x
0 0 0 0 0 0 0 1 x x x
0 0 0 0 0 0 0 0 x x x
0 0 0 0 0 0 0 1 x x x
0 0 0 0 0 0 0 0 x x x
0 0 0 0 0 0 0 1 x x x
0 0 0 0 0 0 0 0 x x x
0 0 0 0 0 0 0 1 x x x
0 0 0 0 0 0 0 0 x x x
0 0 0 0 0 0 0 1 x x x
0 0 0 0 0 0 0 0 x x x
0 0 0 0 0 0 0 1 x x x
0 0 0 0 0 0 0 0 x x x
0 0 0 0 0 0 0 1 x x x
0 0 0 0 0 0 0 0 x x x
0 0 0 0 0 0 0 1 x x x
0 0 0 0 0 0 0 0 x x x
0 0 0 0 0 0 0 1 x x x
0 0 0 0 0 0 0 0 x x x
0 0 0 0 0 0 0 1 x x x
0 0 0 0 0 0 0 0 x x x
0 0 0 0 0 0 0 1 x x x
0 0 0 0 0 0 0 0 x x x
0 0 0 0 0 0 0 1 x x x
0 0 0 0 0 0 0 0 x x x
0 0 0 0 0 0 0 1 x x x
0 0 0 0 0 0 0 0 x x x
0 0 0 0 0 0 0 1 x x x
0 0 0 0 0 0 0 0 x x x
0 0 0 0 0 0 0 1 x x x
0 0 0 0 0 0 0 0 x x x
0 0 0 0 0 0 0 1 x x x
0 0 0 0 0 0 0 0 x x x
0 0 0 0 0 0 0 1 x x x
0 0 0 0 0 0 0 0 x x x
0 0 0 0 0 0 0 1 x x x
0 0 0 0 0 0 0 0 x x x
0 0 0 0 0 0 0 1 x x x
0 0 0 0 0 0 0 0 x x x
0 0 0 0 0 0 0 1 x x x
0 0 0 0 0 0 1 0 1 0 x
0 0 0 0 0 0 1 1 1 0 0
0 0 0 0 0 0 0 0 1 0 0
0 0 0 0 0 0 0 1 1 0 1
0 0 0 0 0 0 0 0 1 0 1
0 0 0 0 0 0 0 1 1 0 0
0 0 0 0 0 0 0 0 1 0 0
0 0 0 0 0 0 0 1 1 0 128
0 0 0 0 0 0 0 0 1 0 128
0 0 0 0 0 0 0 1 1 0 0
0 0 0 0 0 0 0 0 1 0 0
0 0 0 0 0 0 0 1 1 0 0
0 0 0 0 0 0 0 0 1 0 0
0 0 0 0 0 0 0 1 1 0 0
0 0 0 0 0 0 0 0 1 0 0
0 0 0 0 0 0 0 1 1 0 0b10001011
0 0 0 0 0 0 0 0 1 0 0b10001011
0 0 0 0 0 0 0 1 1 0 0
0 0 0 0 0 0 0 0 1 0 0
0 0 0 0 0 0 0 1 1 0 0
0 0 0 0 0 0 0 0 1 0 0
0 0 0 0 0 0 0 1 1 0 0
0 0 0 0 0 0 0 0 1 0 0
0 0 0 0 0 0 0 1 1 0 0
0 0 0 0 0 0 0 0 1 0 0
0 0 0 0 0 0 0 1 1 0 0
0 0 0 0 0 0 0 0 1 0 0
0 0 0 0 0 0 0 1 1 0 0
0 0 0 0 0 0 0 0 1 0 0
0 0 0 0 0 0 0 1 1 0 0
0 0 0 0 0 0 0 0 1 0 0
0 0 0 0 0 0 0 1 1 0 0
0 0 0 0 0 0 0 0 1 0 0
0 0 0 0 0 0 0 1 1 1 x
*/

/* Test case 02_P01T2:
M N progIN reset progLoad start result clk valid done output
0 0 0 0 0 0 0 0 x x x
0 0 0 0 0 0 0 1 x x x
0 0 0 1 0 0 0 0 x x x
0 0 0 1 0 0 0 1 0 0 x
0 0 0 0 0 0 0 0 0 0 x
0 0 0 0 0 0 0 1 0 0 x
0 0 0 0 0 0 0 0 0 0 x
0 0 0 0 0 0 0 1 0 0 x
0 0 0 0 0 0 0 0 0 0 x
0 0 0 0 0 0 0 1 0 0 x
0 0 0 0 0 0 0 0 0 0 x
0 0 0 0 0 0 0 1 0 0 x
0 0 0 0 0 0 0 0 0 0 x
0 0 0 0 0 0 0 1 0 0 x
0 0 0 0 0 0 0 0 0 0 x
0 0 0 0 0 0 0 1 0 0 x
0 0 0 0 0 0 0 0 0 0 x
0 0 0 0 0 0 0 1 0 0 x
0 0 0 0 0 0 0 0 0 0 x
0 0 0 0 0 0 0 1 0 0 x
0 0 0 0 0 0 0 0 0 0 x
0 0 0 0 0 0 0 1 0 0 x
0 0 0 0 0 0 0 0 0 0 x
0 0 0 0 0 0 0 1 0 0 x
0 0 0 0 0 0 0 0 0 0 x
0 0 0 0 0 0 0 1 0 0 x
0 0 0 0 0 0 0 0 0 0 x
0 0 0 0 0 0 0 1 0 0 x
0 0 0 0 0 0 0 0 0 0 x
0 0 0 0 0 0 0 1 0 0 x
0 0 0 0 0 0 0 0 0 0 x
0 0 0 0 0 0 0 1 0 0 x
0 0 0 0 0 0 0 0 0 0 x
0 0 0 0 0 0 0 1 0 0 x
0 0 0 0 0 0 0 0 0 0 x
0 0 0 0 0 0 0 1 0 0 x
0 0 0 0 0 0 0 0 0 0 x
0 0 0 0 0 0 0 1 0 0 x
0 0 0 0 0 0 0 0 0 0 x
0 0 0 0 0 0 0 1 0 0 x
0 0 0 0 0 0 0 0 0 0 x
0 0 0 0 0 0 0 1 0 0 x
0 0 271 0 1 0 0 0 0 0 x
0 0 271 0 1 0 0 1 0 0 x
0 0 565 0 1 0 0 0 0 0 x
0 0 565 0 1 0 0 1 0 0 x
0 0 4352 0 1 0 0 0 0 0 x
0 0 4352 0 1 0 0 1 0 0 x
0 0 2819 0 1 0 0 0 0 0 x
0 0 2819 0 1 0 0 1 0 0 x
0 0 7936 0 1 0 0 0 0 0 x
0 0 7936 0 1 0 0 1 0 0 x
0 0 0 0 0 1 0 0 0 0 x
0 0 0 0 0 1 0 1 0 0 x
0 0 0 0 0 0 0 0 x 0 x
0 0 0 0 0 0 0 1 x 0 x
0 0 0 0 0 0 0 0 x 0 x
0 0 0 0 0 0 0 1 x 0 x
0 0 0 0 0 0 0 0 x 0 x
0 0 0 0 0 0 0 1 x 0 x
0 0 0 0 0 0 0 0 x 0 x
0 0 0 0 0 0 0 1 x 0 x
0 0 0 0 0 0 0 0 x 0 x
0 0 0 0 0 0 0 1 x 0 x
0 0 0 0 0 0 0 0 x 0 x
0 0 0 0 0 0 0 1 x 0 x
0 0 0 0 0 0 0 0 x 0 x
0 0 0 0 0 0 0 1 x 0 x
0 0 0 0 0 0 0 0 x 0 x
0 0 0 0 0 0 0 1 x 0 x
0 0 0 0 0 0 0 0 x 0 x
0 0 0 0 0 0 0 1 x 0 x
0 0 0 0 0 0 0 0 x 0 x
0 0 0 0 0 0 0 1 x 0 x
0 0 0 0 0 0 0 0 x 0 x
0 0 0 0 0 0 0 1 x 0 x
0 0 0 0 0 0 0 0 x 0 x
0 0 0 0 0 0 0 1 x 0 x
0 0 0 0 0 0 0 0 x 0 x
0 0 0 0 0 0 0 1 x 0 x
0 0 0 0 0 0 0 0 x 0 x
0 0 0 0 0 0 0 1 x 0 x
0 0 0 0 0 0 0 0 x 0 x
0 0 0 0 0 0 0 1 x 0 x
0 0 0 0 0 0 0 0 x 0 x
0 0 0 0 0 0 0 1 x 0 x
0 0 0 0 0 0 0 0 x 0 x
0 0 0 0 0 0 0 1 x 0 x
0 0 0 0 0 0 0 0 x 0 x
0 0 0 0 0 0 0 1 x 0 x
0 0 0 0 0 0 0 0 x 0 x
0 0 0 0 0 0 0 1 x 0 x
0 0 0 0 0 0 0 0 x 0 x
0 0 0 0 0 0 0 1 x 0 x
0 0 0 0 0 0 0 0 x 0 x
0 0 0 0 0 0 0 1 x 0 x
0 0 0 0 0 0 0 0 x 0 x
0 0 0 0 0 0 0 1 x 0 x
0 0 0 0 0 0 0 0 x 0 x
0 0 0 0 0 0 0 1 x 0 x
0 0 0 0 0 0 0 0 x 0 x
0 0 0 0 0 0 0 1 x 0 x
0 0 0 0 0 0 0 0 x 0 x
0 0 0 0 0 0 0 1 x 0 x
0 0 0 0 0 0 0 0 x 0 x
0 0 0 0 0 0 0 1 1 0 x
0 0 0 0 0 0 1 0 1 0 x
0 0 0 0 0 0 1 1 1 0 0
0 0 0 0 0 0 0 0 1 0 0
0 0 0 0 0 0 0 1 1 0 0
0 0 0 0 0 0 0 0 1 0 0
0 0 0 0 0 0 0 1 1 0 0
0 0 0 0 0 0 0 0 1 0 0
0 0 0 0 0 0 0 1 1 0 68
0 0 0 0 0 0 0 0 1 0 68
0 0 0 0 0 0 0 1 1 0 0
0 0 0 0 0 0 0 0 1 0 0
0 0 0 0 0 0 0 1 1 0 0
0 0 0 0 0 0 0 0 1 0 0
0 0 0 0 0 0 0 1 1 0 0
0 0 0 0 0 0 0 0 1 0 0
0 0 0 0 0 0 0 1 1 0 0
0 0 0 0 0 0 0 0 1 0 0
0 0 0 0 0 0 0 1 1 0 0
0 0 0 0 0 0 0 0 1 0 0
0 0 0 0 0 0 0 1 1 0 0
0 0 0 0 0 0 0 0 1 0 0
0 0 0 0 0 0 0 1 1 0 0
0 0 0 0 0 0 0 0 1 0 0
0 0 0 0 0 0 0 1 1 0 0
0 0 0 0 0 0 0 0 1 0 0
0 0 0 0 0 0 0 1 1 0 0
0 0 0 0 0 0 0 0 1 0 0
0 0 0 0 0 0 0 1 1 0 0
0 0 0 0 0 0 0 0 1 0 0
0 0 0 0 0 0 0 1 1 0 0
0 0 0 0 0 0 0 0 1 0 0
0 0 0 0 0 0 0 1 1 0 0
0 0 0 0 0 0 0 0 1 0 0
0 0 0 0 0 0 0 1 1 1 x
0 0 0 0 0 0 0 0 1 1 x
0 0 0 0 0 0 0 1 1 1 x
0 0 0 0 0 0 0 0 1 1 x
0 0 0 0 0 0 0 1 1 1 x
0 0 0 0 0 0 1 0 1 X x
0 0 0 0 0 0 1 1 1 X 0
0 0 0 0 0 0 0 0 1 0 0
0 0 0 0 0 0 0 1 1 0 0
0 0 0 0 0 0 0 0 1 0 0
0 0 0 0 0 0 0 1 1 0 0
0 0 0 0 0 0 0 0 1 0 0
0 0 0 0 0 0 0 1 1 0 68
0 0 0 0 0 0 0 0 1 0 68
0 0 0 0 0 0 0 1 1 0 0
0 0 0 0 0 0 0 0 1 0 0
0 0 0 0 0 0 0 1 1 0 0
0 0 0 0 0 0 0 0 1 0 0
0 0 0 0 0 0 0 1 1 0 0
0 0 0 0 0 0 0 0 1 0 0
0 0 0 0 0 0 0 1 1 0 0
0 0 0 0 0 0 0 0 1 0 0
0 0 0 0 0 0 0 1 1 0 0
0 0 0 0 0 0 0 0 1 0 0
0 0 0 0 0 0 0 1 1 0 0
0 0 0 0 0 0 0 0 1 0 0
0 0 0 0 0 0 0 1 1 0 0
0 0 0 0 0 0 0 0 1 0 0
0 0 0 0 0 0 0 1 1 0 0
0 0 0 0 0 0 0 0 1 0 0
0 0 0 0 0 0 0 1 1 0 0
0 0 0 0 0 0 0 0 1 0 0
0 0 0 0 0 0 0 1 1 0 0
0 0 0 0 0 0 0 0 1 0 0
0 0 0 0 0 0 0 1 1 0 0
0 0 0 0 0 0 0 0 1 0 0
0 0 0 0 0 0 0 1 1 0 0
0 0 0 0 0 0 0 0 1 0 0
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*/

/* Test case Almostin1:
M N progIN reset progLoad start result clk valid done output
0 0 0 0 0 0 0 0 x x x
0 0 0 0 0 0 0 1 x x x
0 0 0b0000100000111 0 1 0 0 0 0 0 x
0 0 0b0000100000111 0 1 0 0 1 0 0 x
0 0 0b0001000000100 0 1 0 0 0 0 0 x
0 0 0b0001000000100 0 1 0 0 1 0 0 x
0 0 0b0000000000100 0 1 0 0 0 0 0 x
0 0 0b0000000000100 0 1 0 0 1 0 0 x
0 0 0b0010000000000 0 1 0 0 0 0 0 x
0 0 0b0010000000000 0 1 0 0 1 0 0 x
0 0 0b0100100000010 0 1 0 0 0 0 0 x
0 0 0b0100100000010 0 1 0 0 1 0 0 x
0 0 0b0010100000000 0 1 0 0 0 0 0 x
0 0 0b0010100000000 0 1 0 0 1 0 0 x
0 0 0b1000100000000 0 1 0 0 0 0 0 x
0 0 0b1000100000000 0 1 0 0 1 0 0 x
0 0 0b0101100000000 0 1 0 0 0 0 0 x
0 0 0b0101100000000 0 1 0 0 1 0 0 x
0 0 0b0011000000111 0 1 0 0 0 0 0 x
0 0 0b0011000000111 0 1 0 0 1 0 0 x
0 0 0b1000100000000 0 1 0 0 0 0 0 x
0 0 0b1000100000000 0 1 0 0 1 0 0 x
0 0 0b0101100000000 0 1 0 0 0 0 0 x
0 0 0b0101100000000 0 1 0 0 1 0 0 x
0 0 0b0011000000111 0 1 0 0 0 0 0 x
0 0 0b0011000000111 0 1 0 0 1 0 0 x
0 0 0b1000100000000 0 1 0 0 0 0 0 x
0 0 0b1000100000000 0 1 0 0 1 0 0 x
0 0 0b0101100000000 0 1 0 0 0 0 0 x
0 0 0b0101100000000 0 1 0 0 1 0 0 x
0 0 0b0011000000111 0 1 0 0 0 0 0 x
0 0 0b0011000000111 0 1 0 0 1 0 0 x
0 0 0b1001000000000 0 1 0 0 0 0 0 x
0 0 0b1001000000000 0 1 0 0 1 0 0 x
0 0 0b0101100000001 0 1 0 0 0 0 0 x
0 0 0b0101100000001 0 1 0 0 1 0 0 x
0 0 0b0011000000111 0 1 0 0 0 0 0 x
0 0 0b0011000000111 0 1 0 0 1 0 0 x
0 0 0b1001100000000 0 1 0 0 0 0 0 x
0 0 0b1001100000000 0 1 0 0 1 0 0 x
0 0 0b0101100000010 0 1 0 0 0 0 0 x
0 0 0b0101100000010 0 1 0 0 1 0 0 x
0 0 0b0011000000111 0 1 0 0 0 0 0 x
0 0 0b0011000000111 0 1 0 0 1 0 0 x
0 0 0b1010000000000 0 1 0 0 0 0 0 x
0 0 0b1010000000000 0 1 0 0 1 0 0 x
0 0 0b0101100000011 0 1 0 0 0 0 0 x
0 0 0b0101100000011 0 1 0 0 1 0 0 x
0 0 0b0011000000111 0 1 0 0 0 0 0 x
0 0 0b0011000000111 0 1 0 0 1 0 0 x
0 0 0b1010100000000 0 1 0 0 0 0 0 x
0 0 0b1010100000000 0 1 0 0 1 0 0 x
0 0 0b0101100000100 0 1 0 0 0 0 0 x
0 0 0b0101100000100 0 1 0 0 1 0 0 x
0 0 0b0011000000111 0 1 0 0 0 0 0 x
0 0 0b0011000000111 0 1 0 0 1 0 0 x
0 0 0b1011000000000 0 1 0 0 0 0 0 x
0 0 0b1011000000000 0 1 0 0 1 0 0 x
0 0 0b0101100000101 0 1 0 0 0 0 0 x
0 0 0b0101100000101 0 1 0 0 1 0 0 x
0 0 0b0011000000111 0 1 0 0 0 0 0 x
0 0 0b0011000000111 0 1 0 0 1 0 0 x
0 0 0b1100000000000 0 1 0 0 0 0 0 x
0 0 0b1100000000000 0 1 0 0 1 0 0 x
0 0 0b0101100000110 0 1 0 0 0 0 0 x
0 0 0b0101100000110 0 1 0 0 1 0 0 x
0 0 0b0011000000111 0 1 0 0 0 0 0 x
0 0 0b0011000000111 0 1 0 0 1 0 0 x
0 0 0b1100100000000 0 1 0 0 0 0 0 x
0 0 0b1100100000000 0 1 0 0 1 0 0 x
0 0 0b0101100000111 0 1 0 0 0 0 0 x
0 0 0b0101100000111 0 1 0 0 1 0 0 x
0 0 0b0011000000111 0 1 0 0 0 0 0 x
0 0 0b0011000000111 0 1 0 0 1 0 0 x
0 0 0b1101000000000 0 1 0 0 0 0 0 x
0 0 0b1101000000000 0 1 0 0 1 0 0 x
0 0 0b0101100001000 0 1 0 0 0 0 0 x
0 0 0b0101100001000 0 1 0 0 1 0 0 x
0 0 0b0011000000111 0 1 0 0 0 0 0 x
0 0 0b0011000000111 0 1 0 0 1 0 0 x
0 0 0b1101100000000 0 1 0 0 0 0 0 x
0 0 0b1101100000000 0 1 0 0 1 0 0 x
0 0 0b0101100001001 0 1 0 0 0 0 0 x
0 0 0b0101100001001 0 1 0 0 1 0 0 x
0 0 0b0011000000111 0 1 0 0 0 0 0 x
0 0 0b0011000000111 0 1 0 0 1 0 0 x
0 0 0b1110000000000 0 1 0 0 0 0 0 x
0 0 0b1110000000000 0 1 0 0 1 0 0 x
0 0 0b0101100001010 0 1 0 0 0 0 0 x
0 0 0b0101100001010 0 1 0 0 1 0 0 x
0 0 0b0011000000111 0 1 0 0 0 0 0 x
0 0 0b0011000000111 0 1 0 0 1 0 0 x
0 0 0b1111100000000 0 1 0 0 0 0 0 x
0 0 0b1111100000000 0 1 0 0 1 0 0 x
0 0 0 0 0 1 0 0 0 0 x
0 0 0 0 0 1 0 1 0 0 x
1 1 0 0 0 0 0 0 x x x
1 1 0 0 0 0 0 1 x x x
1 1 0 0 0 0 0 0 x x x
1 1 0 0 0 0 0 1 x x x
1 1 0 0 0 0 0 0 x x x
1 1 0 0 0 0 0 1 x x x
1 1 0 0 0 0 0 0 x x x
1 1 0 0 0 0 0 1 x x x
1 1 0 0 0 0 0 0 x x x
1 1 0 0 0 0 0 1 x x x
1 1 0 0 0 0 0 0 x x x
1 1 0 0 0 0 0 1 x x x
1 1 0 0 0 0 0 0 x x x
1 1 0 0 0 0 0 1 x x x
1 1 0 0 0 0 0 0 x x x
1 1 0 0 0 0 0 1 x x x
1 1 0 0 0 0 0 0 x x x
1 1 0 0 0 0 0 1 x x x
1 1 0 0 0 0 0 0 x x x
1 1 0 0 0 0 0 1 x x x
1 1 0 0 0 0 0 0 x x x
1 1 0 0 0 0 0 1 x x x
1 1 0 0 0 0 0 0 x x x
1 1 0 0 0 0 0 1 x x x
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*/

/* Test case 03_P02T01:
M N progIN reset progLoad start result clk valid done output
0 0 0 0 0 0 0 0 x x x
0 0 0 0 0 0 0 1 x x x
0 0 0 1 0 0 0 0 x x x
0 0 0 1 0 0 0 1 0 0 x
0 0 0 0 0 0 0 0 0 0 x
0 0 0 0 0 0 0 1 0 0 x
0 0 0 0 0 0 0 0 0 0 x
0 0 0 0 0 0 0 1 0 0 x
0 0 0 0 0 0 0 0 0 0 x
0 0 0 0 0 0 0 1 0 0 x
0 0 0 0 0 0 0 0 0 0 x
0 0 0 0 0 0 0 1 0 0 x
0 0 0 0 0 0 0 0 0 0 x
0 0 0 0 0 0 0 1 0 0 x
0 0 0 0 0 0 0 0 0 0 x
0 0 0 0 0 0 0 1 0 0 x
0 0 0 0 0 0 0 0 0 0 x
0 0 0 0 0 0 0 1 0 0 x
0 0 0 0 0 0 0 0 0 0 x
0 0 0 0 0 0 0 1 0 0 x
0 0 0 0 0 0 0 0 0 0 x
0 0 0 0 0 0 0 1 0 0 x
0 0 0 0 0 0 0 0 0 0 x
0 0 0 0 0 0 0 1 0 0 x
0 0 0 0 0 0 0 0 0 0 x
0 0 0 0 0 0 0 1 0 0 x
0 0 0 0 0 0 0 0 0 0 x
0 0 0 0 0 0 0 1 0 0 x
0 0 0 0 0 0 0 0 0 0 x
0 0 0 0 0 0 0 1 0 0 x
0 0 0 0 0 0 0 0 0 0 x
0 0 0 0 0 0 0 1 0 0 x
0 0 0 0 0 0 0 0 0 0 x
0 0 0 0 0 0 0 1 0 0 x
0 0 0 0 0 0 0 0 0 0 x
0 0 0 0 0 0 0 1 0 0 x
0 0 0 0 0 0 0 0 0 0 x
0 0 0 0 0 0 0 1 0 0 x
0 0 0 0 0 0 0 0 0 0 x
0 0 0 0 0 0 0 1 0 0 x
0 0 0 0 0 0 0 0 0 0 x
0 0 0 0 0 0 0 1 0 0 x
0 0 271 0 1 0 0 0 0 0 x
0 0 271 0 1 0 0 1 0 0 x
0 0 566 0 1 0 0 0 0 0 x
0 0 566 0 1 0 0 1 0 0 x
0 0 5888 0 1 0 0 0 0 0 x
0 0 5888 0 1 0 0 1 0 0 x
0 0 3599 0 1 0 0 0 0 0 x
0 0 3599 0 1 0 0 1 0 0 x
0 0 4110 0 1 0 0 0 0 0 x
0 0 4110 0 1 0 0 1 0 0 x
0 0 3856 0 1 0 0 0 0 0 x
0 0 3856 0 1 0 0 1 0 0 x
0 0 7936 0 1 0 0 0 0 0 x
0 0 7936 0 1 0 0 1 0 0 x
0 0 0 0 1 0 0 0 0 0 x
0 0 0 0 1 0 0 1 0 0 x
0 0 0 0 1 0 0 0 0 0 x
0 0 0 0 1 0 0 1 0 0 x
0 0 0 0 1 0 0 0 0 0 x
0 0 0 0 1 0 0 1 0 0 x
0 0 0 0 1 0 0 0 0 0 x
0 0 0 0 1 0 0 1 0 0 x
0 0 0 0 1 0 0 0 0 0 x
0 0 0 0 1 0 0 1 0 0 x
0 0 0 0 1 0 0 0 0 0 x
0 0 0 0 1 0 0 1 0 0 x
0 0 0 0 1 0 0 0 0 0 x
0 0 0 0 1 0 0 1 0 0 x
0 0 0 0 1 0 0 0 0 0 x
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*/

/* Test case 04_P03T01:
M N progIN reset progLoad start result clk valid done output
0 0 0 0 0 0 0 0 x x x
0 0 0 0 0 0 0 1 x x x
0 0 0 1 0 0 0 0 x x x
0 0 0 1 0 0 0 1 0 0 x
0 0 0 0 0 0 0 0 0 0 x
0 0 0 0 0 0 0 1 0 0 x
0 0 0 0 0 0 0 0 0 0 x
0 0 0 0 0 0 0 1 0 0 x
0 0 0 0 0 0 0 0 0 0 x
0 0 0 0 0 0 0 1 0 0 x
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*/

/* Test case 05_P04T01:
M N progIN reset progLoad start result clk valid done output
0 0 0 0 0 0 0 0 x x x
0 0 0 0 0 0 0 1 x x x
0 0 0 1 0 0 0 0 x x x
0 0 0 1 0 0 0 1 0 0 x
0 0 0 0 0 0 0 0 0 0 x
0 0 0 0 0 0 0 1 0 0 x
0 0 0 0 0 0 0 0 0 0 x
0 0 0 0 0 0 0 1 0 0 x
0 0 0 0 0 0 0 0 0 0 x
0 0 0 0 0 0 0 1 0 0 x
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*/

/* Test case 06_P05T01:
M N progIN reset progLoad start result clk valid done output
0 0 0 0 0 0 0 0 x x x
0 0 0 0 0 0 0 1 x x x
0 0 0 1 0 0 0 0 x x x
0 0 0 1 0 0 0 1 0 0 x
0 0 0 0 0 0 0 0 0 0 x
0 0 0 0 0 0 0 1 0 0 x
0 0 0 0 0 0 0 0 0 0 x
0 0 0 0 0 0 0 1 0 0 x
0 0 0 0 0 0 0 0 0 0 x
0 0 0 0 0 0 0 1 0 0 x
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*/

/* Test case 07_P06T02:
M N progIN reset progLoad start result clk valid done output
0 0 0 0 0 0 0 0 x x x
0 0 0 0 0 0 0 1 x x x
0 0 0 1 0 0 0 0 x x x
0 0 0 1 0 0 0 1 0 0 x
0 0 0 0 0 0 0 0 0 0 x
0 0 0 0 0 0 0 1 0 0 x
0 0 0 0 0 0 0 0 0 0 x
0 0 0 0 0 0 0 1 0 0 x
0 0 0 0 0 0 0 0 0 0 x
0 0 0 0 0 0 0 1 0 0 x
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*/

/* Test case 08_P06T2:
M N progIN reset progLoad start result clk valid done output
0 0 0 0 0 0 0 0 x x x
0 0 0 0 0 0 0 1 x x x
0 0 0 1 0 0 0 0 x x x
0 0 0 1 0 0 0 1 0 0 x
0 0 0 0 0 0 0 0 0 0 x
0 0 0 0 0 0 0 1 0 0 x
0 0 0 0 0 0 0 0 0 0 x
0 0 0 0 0 0 0 1 0 0 x
0 0 0 0 0 0 0 0 0 0 x
0 0 0 0 0 0 0 1 0 0 x
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*/
