// Digital circuit Template.dig as structural Verilog
module Template (
  input  D,
  input  Clear,
  input  Clock,
  output Q,
  output Q_2
);

  wire nor_1_out, nor_2_out, nor_3_out, nor_4_out, not_1_out, or_1_out;

  not not_1 (not_1_out, Clock);
  nor nor_1 (nor_1_out, or_1_out, nor_2_out);
  nor nor_2 (nor_2_out, nor_1_out, not_1_out);
  nor nor_3 (nor_3_out, nor_2_out, not_1_out, or_1_out);
  nor nor_4 (nor_4_out, nor_3_out, D);
  or or_1 (or_1_out, nor_4_out, Clear);
  nor nor_5 (Q, nor_2_out, Q_2);
  nor nor_6 (Q_2, Q, nor_3_out);
endmodule
